# Fritzing sketch texecom_pcb_3 (saved by Fritzing 0.9.3b)
circuit board: 4.9cm x 2.25cm
breadboards: 1

parts:
  Part10 = Photon
  U2 = Voltage Regulator [package=to220-adj]
  J1 = Screw terminal - 2 pins [package=THT]
  J2 = Screw terminal - 2 pins [package=THT]
  Part12 = Logic Level Converter
  J4 = female pin header, 2 pins [form="♀ (female)"]
  J5 = female pin header, 7 pins [form="♀ (female)"]
  J3 = female pin header, 7 pins [form="♀ (female)"]

nets:
  N1: Part10.A0, J3.pin6
  N2: Part10.A1, J3.pin5
  N3: Part10.A2, J3.pin4
  N4: Part10.A3, J3.pin3
  N5: Part10.A4, J3.pin2
  N6: Part10.A5, J3.pin1
  N7: Part10.RX, Part12.TX2_LV
  N8: Part10.TX, Part12.RX2_LV
  GND: Part10.GND, U2.OUT, J1.pin1, Part12.GND, J4.pin2, J5.pin7
  N9: Part10.VIN, U2.IN, Part12.HV, J3.pin7
  N10: Part10.D0, J5.pin6
  N11: Part10.D1, J5.pin5
  N12: Part10.D2, J5.pin4
  N13: Part10.D3, J5.pin3
  N14: Part10.D4, J5.pin2
  N15: Part10.D5, J5.pin1
  N16: Part10.RST, J4.pin1
  N17: Part10.3V3, Part12.LV
  N18: U2.ADJ, J1.pin2
  N19: J2.pin1, Part12.RX2_HV
  N20: J2.pin2, Part12.TX2_HV

notes:
  GND
  5V
  RST
