# Fritzing sketch texecom_pcb_5 (saved by Fritzing 0.9.3b)
circuit board: 6.2cm x 2.45cm
circuit board: 6.2cm x 2.45cm
circuit board: 5cm x 2.7cm
breadboards: 1

parts:
  J6 = female pin header, 2 pins [form="♀ (female)"]
  Part13 = Logic Level Converter
  Part14 = Photon
  U3 = Voltage Regulator [package=to220-adj]
  J8 = female pin header, 9 pins [form="♀ (female)"]
  J9 = shrouded pin header, 12 pins [form="♂ (shrouded male)"]
  J11 = female pin header, 9 pins [form="♀ (female)"]
  J12 = female pin header, 2 pins [form="♀ (female)"]
  Part15 = Logic Level Converter
  U4 = Voltage Regulator [package=to220-adj]
  Part18 = Adafruit White 15x7 CharliePlex FeatherWing [part_number="Adafruit #3138"]
  J10 = shrouded pin header, 12 pins [form="♂ (shrouded male)"]
  J13 = shrouded pin header, 12 pins [form="♂ (shrouded male)"]
  J14 = female pin header, 9 pins [form="♀ (female)"]
  J15 = female pin header, 2 pins [form="♀ (female)"]
  Part20 = Logic Level Converter
  U5 = Voltage Regulator [package=to220-adj]
  Part21 = Photon

nets:
  N1: J6.pin1, Part14.RST
  GND: J6.pin2, Part13.GND, Part14.GND, U3.OUT, J9.pin2
  N2: Part13.TX2_LV, Part14.RX
  N3: Part13.RX2_LV, Part14.TX
  N4: Part13.LV, Part14.3V3, J8.pin1
  N5: Part13.HV, Part14.VIN, U3.IN
  N6: Part13.RX2_HV, J9.pin11
  N7: Part13.TX2_HV, J9.pin12
  N8: Part14.D0, J8.pin9, J9.pin7
  N9: Part14.D1, J8.pin8, J9.pin8
  N10: Part14.D2, J8.pin7, J9.pin9
  N11: Part14.D3, J8.pin6, J9.pin10
  N12: Part14.D4, J8.pin5, J9.pin6
  N13: Part14.D5, J8.pin4, J9.pin5
  N14: Part14.D6, J8.pin3, J9.pin4
  N15: Part14.D7, J8.pin2, J9.pin3
  N16: U3.ADJ, J9.pin1
  N17: J11.pin1, Part15.LV, Part18.VCC
  N18: J11.pin2, Part18.SDA, J10.pin3
  N19: J11.pin3, Part18.SCL, J10.pin4
  N20: J11.pin4, Part18.H, J10.pin5
  N21: J11.pin5, Part18.I, J10.pin6
  N22: J11.pin6, Part18.J, J10.pin7
  N23: J11.pin7, Part18.K, J10.pin8
  N24: J11.pin8, Part18.L, J10.pin9
  N25: J11.pin9, Part18.M, J10.pin10
  GND_2: J12.pin1, Part15.GND, U4.OUT, Part18.GND, J10.pin11
  N26: J12.pin2, Part18.RESET
  N27: Part15.TX2_LV, Part18.RX
  N28: Part15.RX2_LV, Part18.TX
  N29: Part15.HV, U4.IN, Part18.USB
  N30: Part15.RX2_HV, J10.pin12
  N31: Part15.TX2_HV, J10.pin1
  N32: U4.ADJ, J10.pin2
  N33: J13.pin1, Part20.TX2_HV
  N34: J13.pin2, U5.ADJ
  N35: J13.pin3, J14.pin2
  N36: J13.pin4, J14.pin3
  N37: J13.pin5, J14.pin4
  N38: J13.pin6, J14.pin5
  N39: J13.pin7, J14.pin6
  N40: J13.pin8, J14.pin7
  N41: J13.pin9, J14.pin8
  N42: J13.pin10, J14.pin9
  N43: J13.pin11, J15.pin1, Part20.GND, U5.OUT
  N44: J13.pin12, Part20.RX2_HV
  N45: J14.pin1, Part21.VIN
  N46: Part20.TX2_LV, Part21.RX
  N47: Part20.RX2_LV, Part21.TX
  N48: Part20.LV, Part21.3V3
  N49: Part20.HV, U5.IN

notes:
  RST
  GND
  D0
  TX
  VE
  D1
  D2
  D3
  D5
  D4
  D6
  D7
  RX

custom parts:
  Adafruit White 15x7 CharliePlex FeatherWing: You wont be able to look away from the mesmerizing patterns created by this Adafruit 15x7 CharliePlex LED Matrix Display FeatherWing. This 15x7 LED display can be paired with any of our Feather boards for a beautiful, bright grid of 105 charlieplexed LEDs. It even comes with a built-in charlieplex driver that is run over I2C. What is particularly nice about this Wing is the I2C LED driver chip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
