# Fritzing sketch texecom_pcb_6 (saved by Fritzing 0.9.3b)
circuit board: 6.22007cm x 3.5cm
breadboards: 1

parts:
  J12 = female pin header, 2 pins [form="♀ (female)"]
  BOB-12009 = Logic Level Converter
  Part18 = Adafruit White 15x7 CharliePlex FeatherWing [part_number="Adafruit #3138"]
  DC3_Box_Header = shrouded pin header, 12 pins [form="♂ (shrouded male)"]
  1-2450A = Voltage Regulator - 5V [package="TO220 [THT]"]
  4116R-1-103LF = IC, DIP package, 16 pins [chip_label=IC]
  4116R-1-333LF = IC, DIP package, 16 pins [chip_label=IC]
  Dev = female pin header, 11 pins [form="♀ (female)"]

nets:
  GND: J12.pin1, BOB-12009.GND, Part18.GND, DC3_Box_Header.pin11, 1-2450A.GND, 4116R-1-103LF.pin9, 4116R-1-103LF.pin10, 4116R-1-103LF.pin11, 4116R-1-103LF.pin12, 4116R-1-103LF.pin13, 4116R-1-103LF.pin14, 4116R-1-103LF.pin15, 4116R-1-103LF.pin16, Dev.pin3
  N1: J12.pin2, Part18.RESET
  N2: BOB-12009.TX2_LV, Part18.TX
  N3: BOB-12009.RX2_LV, Part18.RX
  N4: BOB-12009.LV, Part18.VCC, Dev.pin2
  N5: BOB-12009.HV, Part18.USB, 1-2450A.output_voltage, Dev.pin1
  N6: BOB-12009.RX2_HV, DC3_Box_Header.pin1
  N7: BOB-12009.TX2_HV, DC3_Box_Header.pin12
  N8: Part18.A, 4116R-1-103LF.pin1, 4116R-1-333LF.pin8
  N9: Part18.B, 4116R-1-103LF.pin2, 4116R-1-333LF.pin7
  N10: Part18.C, 4116R-1-103LF.pin3, 4116R-1-333LF.pin6
  N11: Part18.D, 4116R-1-103LF.pin4, 4116R-1-333LF.pin5
  N12: Part18.E, 4116R-1-103LF.pin8, 4116R-1-333LF.pin1
  N13: Part18.F, 4116R-1-103LF.pin7, 4116R-1-333LF.pin2
  N14: Part18.SCK, 4116R-1-103LF.pin6, 4116R-1-333LF.pin3
  N15: Part18.MOSI, 4116R-1-103LF.pin5, 4116R-1-333LF.pin4
  N16: Part18.SDA, Dev.pin11
  N17: Part18.SCL, Dev.pin10
  N18: Part18.H, Dev.pin9
  N19: Part18.I, Dev.pin8
  N20: Part18.J, Dev.pin7
  N21: Part18.K, Dev.pin6
  N22: Part18.L, Dev.pin5
  N23: Part18.M, Dev.pin4
  N24: DC3_Box_Header.pin2, 1-2450A.input_voltage
  N25: DC3_Box_Header.pin3, 4116R-1-333LF.pin9
  N26: DC3_Box_Header.pin4, 4116R-1-333LF.pin10
  N27: DC3_Box_Header.pin5, 4116R-1-333LF.pin11
  N28: DC3_Box_Header.pin6, 4116R-1-333LF.pin12
  N29: DC3_Box_Header.pin7, 4116R-1-333LF.pin13
  N30: DC3_Box_Header.pin8, 4116R-1-333LF.pin14
  N31: DC3_Box_Header.pin9, 4116R-1-333LF.pin15
  N32: DC3_Box_Header.pin10, 4116R-1-333LF.pin16

notes:
  RST
  GND
  19
  TX
  VE
  18
  17
  16
  D13
  D12
  D14
  D15
  RX
  5V 3V GN D7 D6 D5 D4 D3 D2 D1 D0

custom parts:
  Adafruit White 15x7 CharliePlex FeatherWing: You wont be able to look away from the mesmerizing patterns created by this Adafruit 15x7 CharliePlex LED Matrix Display FeatherWing. This 15x7 LED display can be paired with any of our Feather boards for a beautiful, bright grid of 105 charlieplexed LEDs. It even comes with a built-in charlieplex driver that is run over I2C. What is particularly nice about this Wing is the I2C LED driver chip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
